// Logisim project ProjCPU_mem2.circ as structural Verilog: 7 circuits, main circuit CPU
module ULA4 (
  input  [1:0] ULA,
  input  [3:0] Registrador,
  input  [3:0] Operador,
  output [3:0] RESULTADO
);

  wire [3:0] multiplexer_1_out, multiplexer_2_out, Somador, \Subtração ;

  Adder #(.width(4)) adder_1 (.a(Operador), .b(Registrador), .out(Somador));  // open: cin, cout
  Subtractor #(.width(4)) subtractor_1 (.a(Registrador), .b(Operador), .out(\Subtração ));  // open: bin, bout
  Multiplexer #(.width(4), .enable("false")) multiplexer_1 (
    .in0({Operador[2:0], 1'b0}), .in1({1'b0, Operador[3:1]}), .out(multiplexer_1_out), .sel(ULA[1]));
  Multiplexer #(.width(4), .enable("false")) multiplexer_2 (
    .in0(Somador), .in1(\Subtração ), .out(multiplexer_2_out), .sel(ULA[1]));
  Multiplexer #(.width(4), .enable("false")) multiplexer_3 (
    .in0(multiplexer_2_out), .in1(multiplexer_1_out), .out(RESULTADO), .sel(ULA[0]));

  // Other names for the same wires on the sheet: Divisão[2:0] = Operador[3:1]; Multiplicação[3:1] = Operador[2:0]
endmodule

module CPU (
);

  wire Clean_counter, Clean_Reg, Jmp_mem, K0, K1, K2, K3, L0, L1, L2, L3, L4, L5, L6, L7, L8, L9, not_1_out,
       not_2_out, not_3_out, not_4_out, Reg1in, Reg2in, Regout, S0, S1, S2, S3, S4, S5, S6, S7, S8, S9;
  wire [1:0] Ula;
  wire [3:0] HEX0, HEX1, HEX2, HEX3, HEX4, HEX5, multiplexer_1_out, Operando, Result;
  wire [7:0] count8_1_saida;
  wire [15:0] rom_256x16_1_saida;

  Hex_Digit_Display hex_digit_display_1 (.value(HEX5));  // open: dp
  LED u_L9 (.in(L9));
  LED u_L8 (.in(L8));
  // DipSwitch #(.NSwitches(1)) S8: pin names not known; wires that end beside it: S8
  // DipSwitch #(.NSwitches(1)) S9: pin names not known; wires that end beside it: S9
  Hex_Digit_Display hex_digit_display_2 (.value(HEX4));  // open: dp
  Hex_Digit_Display hex_digit_display_3 (.value(HEX3));  // open: dp
  LED u_L6 (.in(L6));
  LED u_L7 (.in(L7));
  // DipSwitch #(.NSwitches(1)) S6: pin names not known; wires that end beside it: S6
  // DipSwitch #(.NSwitches(1)) S5: pin names not known; wires that end beside it: S5
  // DipSwitch #(.NSwitches(1)) S7: pin names not known; wires that end beside it: S7
  Hex_Digit_Display hex_digit_display_4 (.value(HEX2));  // open: dp
  LED u_L4 (.in(L4));
  LED u_L3 (.in(L3));
  LED u_L5 (.in(L5));
  // DipSwitch #(.NSwitches(1)) S4: pin names not known; wires that end beside it: S4
  // DipSwitch #(.NSwitches(1)) S3: pin names not known; wires that end beside it: S3
  Hex_Digit_Display hex_digit_display_5 (.value(HEX1));  // open: dp
  Hex_Digit_Display hex_digit_display_6 (.value(HEX0));  // open: dp
  LED u_L0 (.in(L0));
  LED u_L2 (.in(L2));
  LED u_L1 (.in(L1));
  // DipSwitch #(.NSwitches(1)) S0: pin names not known; wires that end beside it: S0
  // DipSwitch #(.NSwitches(1)) S2: pin names not known; wires that end beside it: S2
  // DipSwitch #(.NSwitches(1)) S1: pin names not known; wires that end beside it: S1
  Button u_K3 (.out(K3));
  Button u_K2 (.out(K2));
  Button u_K1 (.out(K1));
  Button u_K0 (.out(K0));
  Count8 count8_1 (
    .OPERANDO(Operando), .Clear(S0), .Saida(count8_1_saida), .in_2(S9), .Jmp_mem(Jmp_mem),
    .Clean_Counter(Clean_counter));
  Register #(.Select("low")) register_1 (
    .D(count8_1_saida), .Q({L7, L6, L5, L4, L3, L2, L1, L0}), .clk(not_1_out), .clr(not_2_out));  // open: en
  not not_1 (not_1_out, S9);
  not not_2 (not_2_out, S0);
  UC uc_1 (
    .ROM(rom_256x16_1_saida), .Operando(Operando), .ULA(Ula), .Regout(Regout), .Reg1in(Reg1in),
    .Reg2in(Reg2in), .Clean_Reg(Clean_Reg), .Clean_Counter(Clean_counter), .JMP_Mem(Jmp_mem));
  ROM_256x16 rom_256x16_1 (.\Endereço (count8_1_saida), .Clk(S9), .Clear(S0), .saida(rom_256x16_1_saida));
  not not_3 (not_3_out, S9);
  not not_4 (not_4_out, S0);
  Reg4 reg4_1 (.Entrada(Result), .Clock(S9), .Load(Reg1in), .Saida(HEX0), .CLEAR(S0), .Clean_reg(Clean_Reg));
  Register #(.width(16), .Select("low")) register_2 (
    .D(rom_256x16_1_saida), .Q({HEX5, HEX4, HEX3, HEX2}), .clk(not_3_out), .clr(not_4_out));  // open: en
  Reg4 reg4_2 (.Entrada(Result), .Clock(S9), .Load(Reg2in), .Saida(HEX1), .CLEAR(S0), .Clean_reg(Clean_Reg));
  Multiplexer #(.width(4), .enable("false")) multiplexer_1 (
    .in0(HEX1), .in1(HEX0), .out(multiplexer_1_out), .sel(Regout));
  ULA4 ula4_1 (.Registrador(multiplexer_1_out), .RESULTADO(Result), .Operador(Operando), .ULA(Ula));
endmodule

module Count8 (
  input  [3:0] OPERANDO,
  input  in_2,
  input  Clear,
  input  Jmp_mem,
  input  Clean_Counter,
  output [7:0] Saida
);

  wire and_2_out, Clear_all, Clk, Jmp, not_2_out, T2, T3, T4, T5, T6, T7;

  and and_1 (Jmp, Clk, Jmp_mem);
  not not_1 (Clk, in_2);
  and and_2 (and_2_out, Clean_Counter, Clk);
  ffcont ffcont_1 (.OP(OPERANDO[0]), .JMP(Jmp), .IN(1'b1), .OUT(Saida[0]), .Cl(Clear_all), .CK(Clk));
  not not_2 (not_2_out, and_2_out);
  and and_3 (Clear_all, not_2_out, Clear);
  ffcont ffcont_2 (.OP(OPERANDO[1]), .JMP(Jmp), .IN(Saida[0]), .OUT(Saida[1]), .Cl(Clear_all), .CK(Clk));
  and and_4 (T2, Saida[0], Saida[1]);
  ffcont ffcont_3 (.OP(OPERANDO[2]), .JMP(Jmp), .IN(T2), .OUT(Saida[2]), .Cl(Clear_all), .CK(Clk));
  and and_5 (T3, T2, Saida[2]);
  ffcont ffcont_4 (.OP(OPERANDO[3]), .JMP(Jmp), .IN(T3), .OUT(Saida[3]), .Cl(Clear_all), .CK(Clk));
  and and_6 (T4, T3, Saida[3]);
  T_Flip_Flop #(.NegatePresetClear("true")) t_ff_1 (
    .clk(Clk), .T(T4), .Q(Saida[4]), .preset(1'b1), .reset(Clear_all));  // open: Qn
  and and_7 (T5, T4, Saida[4]);
  T_Flip_Flop #(.NegatePresetClear("true")) t_ff_2 (
    .clk(Clk), .T(T5), .Q(Saida[5]), .preset(1'b1), .reset(Clear_all));  // open: Qn
  and and_8 (T6, T5, Saida[5]);
  T_Flip_Flop #(.NegatePresetClear("true")) t_ff_3 (
    .clk(Clk), .T(T6), .Q(Saida[6]), .preset(1'b1), .reset(Clear_all));  // open: Qn
  and and_9 (T7, T6, Saida[6]);
  T_Flip_Flop #(.NegatePresetClear("true")) t_ff_4 (
    .clk(Clk), .T(T7), .Q(Saida[7]), .preset(1'b1), .reset(Clear_all));  // open: Qn

  // Other names for the same wires on the sheet: Q0 = Saida[0]; Q1 = Saida[1]; Q2 = Saida[2]; Q3 = Saida[3];
  //   Q4 = Saida[4]; Q5 = Saida[5]; Q6 = Saida[6]; Q7 = Saida[7]
endmodule

module Reg4 (
  input  [3:0] Entrada,
  input  Clock,
  input  Load,
  input  CLEAR,
  input  Clean_reg,
  output [3:0] Saida
);

  wire and_1_out, multiplexer_1_out, multiplexer_2_out, multiplexer_3_out, multiplexer_4_out, not_1_out,
       not_2_out, or_1_out;

  not not_1 (not_1_out, Clock);
  and and_1 (and_1_out, not_1_out, Clean_reg);
  Multiplexer #(.enable("false")) multiplexer_1 (.in0(Saida[3]), .in1(Entrada[3]), .out(multiplexer_1_out), .sel(Load));
  not not_2 (not_2_out, CLEAR);
  or or_1 (or_1_out, not_2_out, and_1_out);
  D_Flip_Flop d_ff_1 (.clk(not_1_out), .D(multiplexer_1_out), .Q(Saida[3]), .reset(or_1_out));  // open: Qn, preset
  Multiplexer #(.enable("false")) multiplexer_2 (.in0(Saida[2]), .in1(Entrada[2]), .out(multiplexer_2_out), .sel(Load));
  D_Flip_Flop d_ff_2 (.clk(not_1_out), .D(multiplexer_2_out), .Q(Saida[2]), .reset(or_1_out));  // open: Qn, preset
  Multiplexer #(.enable("false")) multiplexer_3 (.in0(Saida[1]), .in1(Entrada[1]), .out(multiplexer_3_out), .sel(Load));
  D_Flip_Flop d_ff_3 (.clk(not_1_out), .D(multiplexer_3_out), .Q(Saida[1]), .reset(or_1_out));  // open: Qn, preset
  Multiplexer #(.enable("false")) multiplexer_4 (.in0(Saida[0]), .in1(Entrada[0]), .out(multiplexer_4_out), .sel(Load));
  D_Flip_Flop d_ff_4 (.clk(not_1_out), .D(multiplexer_4_out), .Q(Saida[0]), .reset(or_1_out));  // open: Qn, preset
endmodule

module UC (
  input  [15:0] ROM,
  output [3:0] Operando,
  output [1:0] ULA,
  output Regout,
  output Clean_Reg,
  output Clean_Counter,
  output JMP_Mem,
  output Reg1in,
  output Reg2in
);

  wire not_1_out, not_2_out;

  not not_1 (not_1_out, ROM[13]);
  and and_1 (Reg1in, not_1_out, ROM[12]);
  and and_2 (Reg2in, ROM[13], not_2_out);
  not not_2 (not_2_out, ROM[12]);
  and and_3 (Clean_Reg, ROM[10], ~ROM[11]);  // AND_Gate
  and and_4 (Clean_Counter, ~ROM[10], ROM[11]);  // AND_Gate
  and and_5 (JMP_Mem, ROM[10], ROM[11]);

  assign Operando = ROM[3:0];
  assign Regout = ROM[14];
  assign ULA = ROM[9:8];

  // Other names for the same wires on the sheet: JMP[1:0] = ROM[11:10]; Regin[1:0] = ROM[13:12]
endmodule

module ffcont (
  input  OP,
  input  CK,
  input  JMP,
  input  IN,
  input  Cl,
  output OUT
);

  wire and_1_out, nand_1_out, or_1_out;

  nand nand_1 (nand_1_out, JMP, OP);
  T_Flip_Flop #(.NegatePresetClear("true")) t_ff_1 (
    .clk(CK), .T(IN), .Q(OUT), .preset(nand_1_out), .reset(and_1_out));  // open: Qn
  and and_1 (and_1_out, or_1_out, Cl);
  or or_1 (or_1_out, OP, ~JMP);  // OR_Gate
endmodule

module ROM_256x16 (
  input  [7:0] \Endereço ,
  input  Clk,
  input  Clear,
  output [15:0] saida
);

  wire not_1_out;
  wire [15:0] rom_1_data;

  ROM #(.dataWidth(16), .Select("low")) rom_1 (.addr(\Endereço ), .data(rom_1_data));
  Register #(.width(16), .Select("low")) register_1 (
    .D(rom_1_data), .Q(saida), .clk(Clk), .clr(not_1_out));  // open: en
  not not_1 (not_1_out, Clear);

  // Notes on the sheet:
  //   contents of rom_1 (hex, n*v repeats v):
  //   6004 9102 6201 6305 9002 6002 9003 400 c0d 4*0 9002 6302 6101 9302 6200 6003 800
endmodule
